# Fritzing sketch indoor farming wirth pcb 2 (saved by Fritzing 0.9.3b)

parts:
  U1 = ESP32-38PinWide [part_number=ESP32-38PinWide]
  LCD2004-I2C1 = LCD2004-I2C
  Part1 = GUVA-S12SD UV Light Sensor
  U2 = 2-Channel 5v Relay Shield [package=relay-2ch5v10a]
  Part2 = Soil Moisture Sensor
  WATER_PUMP1 = water pump/motor  # not connected
  DHT1 = Humidity and Temperature Sensor DHT11
  WATER_PUMP2 = water pump/motor  # not connected
  U3 = ESP32-38PinWide [part_number=ESP32-38PinWide]
  JP1 = Header 1 [package=1x01_offset]
  JP2 = Header 1 [package=1x01_offset]
  JP3 = Header 1 [package=1x01_offset]  # not connected
  JP4 = Header 1 [package=1x01_offset]
  JP5 = Header 1 [package=1x01_offset]
  JP6 = Header 1 [package=1x01_offset]
  JP7 = Header 1 [package=1x01_offset]
  JP8 = Header 1 [package=1x01_offset]
  JP9 = Header 1 [package=1x01_offset]
  JP10 = Header 1 [package=1x01_offset]
  JP11 = Header 1 [package=1x01_offset]
  Part3 = JeePlug experimenter's board
  Part4 = JeePlug experimenter's board
  U4 = 2-Channel 5v Relay Shield [package=relay-2ch5v10a]
  WATER_PUMP3 = water pump/motor  # not connected
  WATER_PUMP4 = water pump/motor  # not connected
  U5 = ESP32-38PinWide [part_number=ESP32-38PinWide]
  DHT2 = Humidity and Temperature Sensor DHT11
  J2 = Camdenboss CTB0158-2 [part_number=CTB0158-2 package=THT]
  WATER_PUMP6 = water pump/motor  # not connected
  DHT3 = Humidity and Temperature Sensor DHT11
  U6 = ESP32-38PinWide [part_number=ESP32-38PinWide]
  LCD2004-I2C2 = LCD2004-I2C
  U7 = 2-Channel 5v Relay Shield [package=relay-2ch5v10a]
  Part6 = Soil Moisture Sensor
  J3 = Camdenboss CTB0158-2 [part_number=CTB0158-2 package=THT]
  LED1 = LED - 3mm [color="Red (633nm)" package="3 mm [THT]"]
  J4 = Camdenboss CTB0158-2 [part_number=CTB0158-2 package=THT]

nets:
  VCC: U1.3.3, Part2.VCC, DHT1.Vcc
  N1: U1.GPIO32, Part2.SIG
  N2: U1.GPIO33, Part1.Out
  N3: U1.GPIO26, U2.IN1
  N4: U1.GPIO27, U2.IN2
  GND: U1.GND, LCD2004-I2C1.GND, Part1.GND, U2.GND, Part2.GND, DHT1.GND_2
  VCC_2: U1.VIN, LCD2004-I2C1.VCC, Part1.5V, U2.VCC
  N5: U1.GPIO2, DHT1.Data-signal
  N6: U1.GPIO21, LCD2004-I2C1.SDA
  N7: U1.GPIO22, LCD2004-I2C1.SCL
  N8: U2.K1-In, U2.K2-In, J2.terminal_1
  N9: U3.GPIO32, JP7.1
  N10: U3.GPIO26, U4.IN2
  N11: U3.GPIO27, U4.IN1
  N12: U3.GPIO4, JP6.1
  N13: U3.GPIO21, JP10.1
  N14: U3.GPIO22, JP8.1
  N15: JP1.1, Part3.N$8, U4.VCC
  N16: JP2.1, Part4.N$9, U4.GND
  N17: JP4.1, JP9.1, Part4.N$24
  N18: JP5.1, JP11.1, Part3.N$26
  N19: U5.3.3, DHT2.Vcc
  N20: U5.GND, DHT2.GND_1
  N21: U5.GPIO4, DHT2.Data-signal
  VCC_3: DHT3.Vcc, U6.3.3, Part6.VCC
  N22: DHT3.Data-signal, U6.GPIO2
  GND_2: DHT3.GND_2, U6.GND, LCD2004-I2C2.GND, U7.GND, Part6.GND
  N23: U6.GPIO32, Part6.SIG
  N24: U6.GPIO26, U7.IN1
  N25: U6.GPIO27, U7.IN2
  VCC_4: U6.VIN, LCD2004-I2C2.VCC, U7.VCC
  N26: U6.GPIO21, LCD2004-I2C2.SDA
  N27: U6.GPIO22, LCD2004-I2C2.SCL
  N28: U7.K1-In, J4.terminal_1
  N29: U7.K1-On, LED1.cathode
  N30: U7.K2-In, J3.terminal_1
  N31: LED1.anode, J4.terminal_2

notes:
  Yang kurang:
  -soil moisture-motor
  -external psu
  moisture
  DHT
  LCD
  GND
  VCC
  SDA
  SCL
  OUT
  AO
  DO
  anggap aja gnd
  V+ DC
  V- DC
  ceritanya lampu UV AC 220V
  L AC
  N AC

custom parts:
  ESP32-38PinWide: Generic 38-Pin ESP32 with wide format (only access to one side of pins on a breadboard) based on Stephen Lilley's HiLetgo ESP-WROOM-32 ESP32 ESP-32S Development Board.
  LCD2004-I2C: A standard character display with 4x20 characters. Comes in many colors with LCM2004 IIC attached.
  GUVA-S12SD UV Light Sensor: Extend your light-sensing spectrum with this analog UV sensor module. It uses a UV photodiode, which can detect the 240-370nm range of light (which covers UVB and most of UVA spectrum). The signal level from the photodiode is very small, in the nano-ampere level, so we tossed on an opamp to amplify the signal to a more manageable volt-level.
  2-Channel 5v Relay Shield: 2 Channel 5v Relay Shield w. 2x SPD-06VDC-SD-C
  water pump/motor: WATER PUMP BY ARDUBLOCKTR
  Humidity and Temperature Sensor DHT11: Digital relative humidity & temperature sensor DHT11
